# Fritzing sketch ir3 (saved by Fritzing 0.9.3b)
breadboards: 1

parts:
  IC1 = IC, DIP package, 20 pins [chip_label=ATtiny4313]
  X1 = USB Connectors [package=usb-b-smt]
  Fuse_500mA = Resettable Fuse PTC [package=ptc]
  part = Electrolytic Capacitor [capacitance=100µF package="200 mil [THT, electrolytic]"]
  part_2 = Resistor [tolerance=±5% resistance=3.3k package=THT]
  LED-PWR = LED - 5mm [color="Red (633nm)" package="5 mm [THT]"]
  part_3 = Ceramic Capacitor [capacitance=100nF package="100 mil [THT, multilayer]"]
  U1 = RS232 Transceiver [package=dil16]
  1μF = Tantalum Capacitor [capacitance=1μF package="100 mil [THT, tantalum]"]
  1μF_2 = Tantalum Capacitor [capacitance=1μF package="100 mil [THT, tantalum]"]
  1μF_3 = Tantalum Capacitor [capacitance=1μF package="100 mil [THT, tantalum]"]
  1μF_4 = Tantalum Capacitor [capacitance=1μF package="100 mil [THT, tantalum]"]
  X2 = DB9 Connector [package=db9]
  part_4 = Ceramic Capacitor [capacitance=100nF package="100 mil [THT, multilayer]"]
  U2 = AVR 10-pin ICSP Header [package=avr_icsp]
  part_5 = Resistor [tolerance=±5% resistance=4.7 package=THT]
  part_6 = Ceramic Capacitor [capacitance=100nF package="100 mil [THT, multilayer]"]
  part_7 = Resistor [tolerance=±5% resistance=1.5k package=THT]
  LED-NAK = LED - 5mm [color="Red (633nm)" package="5 mm [THT]"]
  part_8 = Resistor [tolerance=±5% resistance=1.5k package=THT]
  LED-ACK = LED - 5mm [color="Green (565nm)" package="5 mm [THT]"]
  part_9 = Resistor [tolerance=±5% resistance=1.5k package=THT]
  LED-RCV = LED - 5mm [color="Yellow (592nm)" package="5 mm [THT]"]
  IR1 = TSOP312.., 314.. [package=THT]
  part_10 = Ceramic Capacitor [capacitance=100nF package="100 mil [THT, multilayer]"]
  part_11 = Resistor [tolerance=±5% resistance=100 package=THT]

nets:
  N1: IC1.pin1, U2.6, part_5.Pin_0, part_6.1
  N2: IC1.pin2, U1.R1OUT
  N3: IC1.pin3, U1.T1IN
  N4: IC1.pin6, LED-NAK.anode
  N5: IC1.pin7, LED-ACK.anode
  N6: IC1.pin8, LED-RCV.anode
  N7: IC1.pin9, IR1.Data
  GND: IC1.pin10, X1.GND, part.-, part_2.Pin_1, part_3.0, U1.GND, 1μF_3.+, 1μF_4.-, X2.1, part_4.1, U2.2, U2.5, U2.7, U2.9, part_6.0, part_7.Pin_1, part_8.Pin_1, part_9.Pin_1, IR1.GND, part_10.1
  N8: IC1.pin17, U2.1
  N9: IC1.pin18, U2.10
  N10: IC1.pin19, U2.8
  N11: IC1.pin20, Fuse_500mA.1, part.+, LED-PWR.anode, part_3.1, U1.VCC, part_4.0, U2.3, part_5.Pin_1, part_11.Pin_1
  N12: X1.D+, Fuse_500mA.2
  N13: part_2.Pin_0, LED-PWR.cathode
  N14: U1.C1+, 1μF.+
  N15: U1.V+, 1μF_4.+
  N16: U1.C1-, 1μF.-
  N17: U1.C2+, 1μF_2.+
  N18: U1.C2-, 1μF_2.-
  N19: U1.V-, 1μF_3.-
  N20: U1.R1IN, X2.3
  N21: U1.T1OUT, X2.4
  N22: part_7.Pin_0, LED-NAK.cathode
  N23: part_8.Pin_0, LED-ACK.cathode
  N24: part_9.Pin_0, LED-RCV.cathode
  N25: IR1.Vs, part_10.0, part_11.Pin_0
